# Fritzing sketch d1mini-openmv (saved by Fritzing 0.9.3b)
circuit board: 3.56cm x 2.04cm

parts:
  3V_A0_D4_D3_CS_SCK_SO_SI = female alternating pin header, 8 pins [form="♀ (female)"]
  G_5V_SCL_SDA_D0_--_--_RST = female alternating pin header, 8 pins [form="♀ (female)"]
  5V_GND_D4_D3_D2_D1_--_-- = female alternating pin header, 8 pins [form="♀ (female)"]
  3V_D8_D7_D6_D5_D0_A0_RST = female alternating pin header, 8 pins [form="♀ (female)"]

nets:
  N1: 3V_A0_D4_D3_CS_SCK_SO_SI.pin1, 3V_D8_D7_D6_D5_D0_A0_RST.pin5
  N2: 3V_A0_D4_D3_CS_SCK_SO_SI.pin2, 3V_D8_D7_D6_D5_D0_A0_RST.pin6
  N3: 3V_A0_D4_D3_CS_SCK_SO_SI.pin3, 3V_D8_D7_D6_D5_D0_A0_RST.pin4
  N4: 3V_A0_D4_D3_CS_SCK_SO_SI.pin4, 3V_D8_D7_D6_D5_D0_A0_RST.pin7
  N5: 3V_A0_D4_D3_CS_SCK_SO_SI.pin5, 5V_GND_D4_D3_D2_D1_--_--.pin5
  N6: 3V_A0_D4_D3_CS_SCK_SO_SI.pin6, 5V_GND_D4_D3_D2_D1_--_--.pin6
  N7: 3V_A0_D4_D3_CS_SCK_SO_SI.pin7, 3V_D8_D7_D6_D5_D0_A0_RST.pin2
  N8: 3V_A0_D4_D3_CS_SCK_SO_SI.pin8, 3V_D8_D7_D6_D5_D0_A0_RST.pin8
  N9: G_5V_SCL_SDA_D0_--_--_RST.pin1, 3V_D8_D7_D6_D5_D0_A0_RST.pin1
  N10: G_5V_SCL_SDA_D0_--_--_RST.pin4, 3V_D8_D7_D6_D5_D0_A0_RST.pin3
  N11: G_5V_SCL_SDA_D0_--_--_RST.pin5, 5V_GND_D4_D3_D2_D1_--_--.pin4
  N12: G_5V_SCL_SDA_D0_--_--_RST.pin6, 5V_GND_D4_D3_D2_D1_--_--.pin3
  N13: G_5V_SCL_SDA_D0_--_--_RST.pin7, 5V_GND_D4_D3_D2_D1_--_--.pin8
  N14: G_5V_SCL_SDA_D0_--_--_RST.pin8, 5V_GND_D4_D3_D2_D1_--_--.pin7
